# Fritzing sketch circuit diagram (saved by Fritzing 0.9.3b)

parts:
  Part1 = Arduino Mega 2560 (Rev3)
  Part2 = Huskylens  # not connected
  S1 = H-Bridge with L298N
  M1 = DC Motor
  M3 = DC Motor
  kEYPAD_MATRICIAL_1 = KEYPAD 4x3
  BATT1 = LiPoly Battery (1300mAh)
  VCC1 = Battery block 9V

nets:
  N1: Part1.D17_PWM/RX2, S1.IN2
  N2: Part1.D16_PWM/TX2, S1.IN1
  N3: Part1.D15/RX3, S1.IN4
  N4: Part1.D14/TX3, S1.IN3
  N5: Part1.D13_PWM, S1.ENA
  N6: Part1.D12_PWM, S1.ENB
  N7: Part1.D9_PWM, kEYPAD_MATRICIAL_1.arrow4
  N8: Part1.D8_PWM, kEYPAD_MATRICIAL_1.arrow3
  N9: Part1.GND, VCC1.-
  N10: Part1.VIN, VCC1.+
  N11: Part1.D3_PWM, kEYPAD_MATRICIAL_1.col1
  N12: Part1.D4_PWM, kEYPAD_MATRICIAL_1.arrow1
  N13: Part1.D5_PWM, kEYPAD_MATRICIAL_1.col2
  N14: Part1.D6_PWM, kEYPAD_MATRICIAL_1.arrow2
  N15: Part1.D7_PWM, kEYPAD_MATRICIAL_1.col3
  N16: S1.12V, BATT1.positive
  N17: S1.GND, BATT1.negative
  N18: S1.M1-01, M3.pin_2
  N19: S1.M1-02, M3.pin_1
  N20: S1.M2-01, M1.pin_2
  N21: S1.M2-02, M1.pin_1

custom parts:
  Huskylens: some AI cam
  H-Bridge with L298N: h-bridge
  KEYPAD 4x3: KEYPAD matricial de 12 botones, 4 filas x 3 columnas
  LiPoly Battery (1300mAh): Lithium Ion Polymer Battery (1300mAh)
